// Logisim project 161044119_hw3.circ as structural Verilog: 2 circuits, main circuit main
module main (
  input  a,
  output x,
  output y,
  output z
);

  wire and_1_out, and_2_out, and_3_out, and_4_out, and_5_out, and_6_out, and_7_out, and_8_out, and_9_out,
       and_10_out, and_11_out, and_12_out, and_13_out, and_14_out, and_15_out, CLOCK_out, n0_out, n1_out,
       n2_out, not_1_out, not_2_out, not_3_out, not_4_out, not_5_out, not_6_out, not_7_out, not_8_out,
       not_9_out, not_10_out, not_11_out, not_12_out, not_13_out, not_14_out, not_15_out, not_16_out,
       not_17_out, not_18_out, not_19_out, or_1_out, or_2_out, STATE_s0, STATE_s1, STATE_s2, xor_1_out,
       xor_2_out;

  Clock CLOCK (.out(CLOCK_out));
  state_register STATE (
    .clk(CLOCK_out), .n2(n2_out), .n1(n1_out), .n0(n0_out), .s2(STATE_s2), .s1(STATE_s1), .s0(STATE_s0));
  not not_1 (not_1_out, STATE_s2);
  not not_2 (not_2_out, STATE_s1);
  not not_3 (not_3_out, STATE_s2);
  not not_4 (not_4_out, a);
  not not_5 (not_5_out, STATE_s1);
  not not_6 (not_6_out, a);
  not not_7 (not_7_out, STATE_s0);
  not not_8 (not_8_out, STATE_s1);
  not not_9 (not_9_out, STATE_s2);
  not not_10 (not_10_out, a);
  not not_11 (not_11_out, STATE_s0);
  not not_12 (not_12_out, STATE_s0);
  not not_13 (not_13_out, STATE_s1);
  not not_14 (not_14_out, STATE_s2);
  not not_15 (not_15_out, STATE_s2);
  not not_16 (not_16_out, STATE_s1);
  not not_17 (not_17_out, STATE_s1);
  not not_18 (not_18_out, STATE_s2);
  xor xor_1 (xor_1_out, STATE_s1, STATE_s0);
  or or_1 (or_1_out, not_1_out, and_1_out);
  and and_1 (and_1_out, STATE_s2, not_2_out);
  xor xor_2 (xor_2_out, a, STATE_s0);
  and and_2 (and_2_out, not_3_out, STATE_s1);
  not not_19 (not_19_out, STATE_s0);
  or or_2 (or_2_out, not_19_out, and_3_out);
  and and_3 (and_3_out, STATE_s0, not_4_out);
  and and_4 (and_4_out, a, not_5_out, STATE_s0);
  and and_5 (and_5_out, not_6_out, STATE_s2, STATE_s1, not_7_out);
  and and_6 (and_6_out, STATE_s2, not_8_out);
  and and_7 (and_7_out, a, not_9_out, STATE_s1, STATE_s0);
  and and_8 (and_8_out, not_10_out, STATE_s2, STATE_s1, not_11_out);
  and and_9 (and_9_out, STATE_s1, not_12_out);
  or u_x (x, and_9_out, and_10_out);
  and and_10 (and_10_out, STATE_s2, not_13_out, STATE_s0);
  and and_11 (and_11_out, not_14_out, STATE_s1);
  or u_y (y, and_11_out, and_12_out);
  and and_12 (and_12_out, not_15_out, not_16_out, STATE_s0);
  and and_13 (and_13_out, STATE_s2, not_17_out);
  or u_z (z, and_13_out, and_14_out);
  and and_14 (and_14_out, not_18_out, xor_1_out);
  and n0 (n0_out, or_1_out, xor_2_out);
  and and_15 (and_15_out, and_2_out, or_2_out);
  or n2 (n2_out, and_6_out, and_7_out, and_8_out);
  or n1 (n1_out, and_15_out, and_4_out, and_5_out);

  // Notes on the sheet:
  //   s2
  //   s1
  //   s0
endmodule

module state_register (
  input  clk,
  input  n2,
  input  n1,
  input  n0,
  output s2,
  output s1,
  output s0
);

  D_Flip_Flop d_ff_1 (.clk(clk), .D(n2), .Q(s2), .en(1'b1));  // open: Qn, preset, reset
  D_Flip_Flop d_ff_2 (.clk(clk), .D(n1), .Q(s1), .en(1'b1));  // open: Qn, preset, reset
  D_Flip_Flop d_ff_3 (.clk(clk), .D(n0), .Q(s0), .en(1'b1));  // open: Qn, preset, reset
endmodule
