// Logisim project 161044119_hw4.circ as structural Verilog: 2 circuits, main circuit main
module main (
  input  I5,
  input  I4,
  input  I3,
  input  I2,
  input  I1,
  input  I0,
  input  cl,
  input  ld,
  input  sw,
  output Q5,
  output Q4,
  output Q3,
  output Q2,
  output Q1,
  output Q0
);

  wire clock_out, multiplexer_1_out, multiplexer_2_out, multiplexer_3_out, multiplexer_4_out,
       multiplexer_5_out, multiplexer_6_out;
  wire [1:0] combinational_circuit_s0;

  combinational_circuit combinational_circuit (
    .cl(cl), .ld(ld), .sw(sw), .s1(combinational_circuit_s0[1]), .s0(combinational_circuit_s0[0]));
  Clock clock (.out(clock_out));
  Multiplexer #(.select(2)) multiplexer_1 (
    .in0(Q5), .in1(1'b0), .in2(I5), .in3(Q4), .out(multiplexer_1_out), .sel(combinational_circuit_s0));  // open: en
  Multiplexer #(.select(2)) multiplexer_2 (
    .in0(Q4), .in1(1'b0), .in2(I4), .in3(Q5), .out(multiplexer_2_out), .sel(combinational_circuit_s0));  // open: en
  Multiplexer #(.select(2)) multiplexer_3 (
    .in0(Q3), .in1(1'b0), .in2(I3), .in3(Q2), .out(multiplexer_3_out), .sel(combinational_circuit_s0));  // open: en
  Multiplexer #(.select(2)) multiplexer_4 (
    .in0(Q2), .in1(1'b0), .in2(I2), .in3(Q3), .out(multiplexer_4_out), .sel(combinational_circuit_s0));  // open: en
  Multiplexer #(.select(2)) multiplexer_5 (
    .in0(Q1), .in1(1'b0), .in2(I1), .in3(Q0), .out(multiplexer_5_out), .sel(combinational_circuit_s0));  // open: en
  Multiplexer #(.select(2)) multiplexer_6 (
    .in0(Q0), .in1(1'b0), .in2(I0), .in3(Q1), .out(multiplexer_6_out), .sel(combinational_circuit_s0));  // open: en
  D_Flip_Flop d_ff_1 (.clk(clock_out), .D(multiplexer_1_out), .Q(Q5));  // open: Qn, preset, en, reset
  D_Flip_Flop d_ff_2 (.D(multiplexer_2_out), .Q(Q4));  // open: clk, Qn, preset, en, reset
  D_Flip_Flop d_ff_3 (.D(multiplexer_3_out), .Q(Q3));  // open: clk, Qn, preset, en, reset
  D_Flip_Flop d_ff_4 (.D(multiplexer_4_out), .Q(Q2));  // open: clk, Qn, preset, en, reset
  D_Flip_Flop d_ff_5 (.D(multiplexer_5_out), .Q(Q1));  // open: clk, Qn, preset, en, reset
  D_Flip_Flop d_ff_6 (.D(multiplexer_6_out), .Q(Q0));  // open: clk, Qn, preset, en, reset

  // Notes on the sheet:
  //   s1
  //   s0
endmodule

module combinational_circuit (
  input  cl,
  input  ld,
  input  sw,
  output s1,
  output s0
);

  wire and_1_out, and_2_out, not_1_out, not_2_out;

  not not_1 (not_1_out, cl);
  and and_1 (and_1_out, not_1_out, ld);
  not not_2 (not_2_out, ld);
  or or_1 (s1, and_1_out, and_2_out);
  and and_2 (and_2_out, not_2_out, not_1_out, sw);
  or or_2 (s0, and_2_out, cl);
endmodule
