// Logisim project 161044119.circ as structural Verilog: 2 circuits, main circuit main
module main (
  input  A,
  input  B,
  input  C,
  input  D,
  output F,
  output G
);

  circuit circuit_1 (.A(A), .B(B), .C(C), .D(D), .F(F), .G(G));
endmodule

module circuit (
  input  A,
  input  B,
  input  C,
  input  D,
  output F,
  output G
);

  wire not_1_out, not_2_out, not_3_out, not_4_out;

  not not_1 (not_1_out, A);
  not not_2 (not_2_out, B);
  not not_3 (not_3_out, C);
  not not_4 (not_4_out, D);
  and and_1 (F, not_2_out, not_4_out);
  and and_2 (G, not_2_out, not_1_out, not_3_out);
endmodule
