// Logisim project 161044119.circ as structural Verilog: 2 circuits, main circuit main
module main (
  input  a,
  input  b,
  output x
);

  wire a_prime_2_out, a_prime_out, and_1_out, and_2_out, and_3_out, and_4_out, and_5_out, and_6_out,
       and_7_out, and_8_out, clk_out, n0_out, n1_out, or_1_out, or_2_out, s0_prime_out, s1_prime_out,
       s1_s0_prime_out, state_register_2bit_1_s0;

  Clock clk (.out(clk_out));
  state_register_2bit state_register_2bit_1 (
    .clk(clk_out), .n1(n1_out), .n0(n0_out), .s1(x), .s0(state_register_2bit_1_s0));
  not s1_prime (s1_prime_out, x);
  not s0_prime (s0_prime_out, state_register_2bit_1_s0);
  not a_prime (a_prime_out, a);
  not a_prime_2 (a_prime_2_out, a);
  and and_1 (and_1_out, a, b);
  and and_2 (and_2_out, s0_prime_out, a_prime_out);
  and and_3 (and_3_out, state_register_2bit_1_s0, s1_prime_out, a);
  and s1_s0_prime (s1_s0_prime_out, s0_prime_out, x);
  or or_1 (or_1_out, a_prime_2_out, and_1_out);
  and and_4 (and_4_out, b, state_register_2bit_1_s0, x);
  and and_5 (and_5_out, a, b, s1_prime_out);
  or or_2 (or_2_out, and_2_out, state_register_2bit_1_s0);
  and and_6 (and_6_out, s1_s0_prime_out, or_1_out);
  and and_7 (and_7_out, b, x);
  and and_8 (and_8_out, and_7_out, or_2_out);
  or n1 (n1_out, and_3_out, and_6_out, and_4_out);
  or n0 (n0_out, and_5_out, and_8_out);
endmodule

module state_register_2bit (
  input  clk,
  input  n1,
  input  n0,
  output s1,
  output s0
);

  D_Flip_Flop d_ff_1 (.clk(clk), .D(n1), .Q(s1), .en(1'b1));  // open: Qn, preset, reset
  D_Flip_Flop d_ff_2 (.clk(clk), .D(n0), .Q(s0), .en(1'b1));  // open: Qn, preset, reset
endmodule
