// Logisim project 161044119_lab5.circ as structural Verilog: 2 circuits, main circuit main
module main (
  input  req,
  input  p3s,
  input  p7s,
  input  p37s,
  output resetT
);

  wire and_1_out, and_2_out, and_3_out, and_4_out, and_5_out, and_6_out, and_7_out, and_9_out, and_10_out,
       and_11_out, and_12_out, and_13_out, and_14_out, and_15_out, clock_1_out, not_1_out, not_2_out,
       not_3_out, not_4_out, not_5_out, not_6_out, not_7_out, not_8_out, not_9_out, not_10_out, not_11_out,
       not_12_out, not_13_out, not_14_out, not_15_out, not_16_out, not_17_out, not_18_out, not_19_out,
       not_20_out, not_21_out, or_1_out, or_2_out, or_3_out, state_register_2bit_1_s0,
       state_register_2bit_1_s1;

  Clock clock_1 (.out(clock_1_out));
  state_register_2bit state_register_2bit_1 (
    .clk(clock_1_out), .s1(state_register_2bit_1_s1), .s0(state_register_2bit_1_s0));  // open: n1, n0
  not not_1 (not_1_out, state_register_2bit_1_s1);
  not not_2 (not_2_out, state_register_2bit_1_s0);
  not not_3 (not_3_out, p37s);
  not not_4 (not_4_out, state_register_2bit_1_s1);
  not not_5 (not_5_out, state_register_2bit_1_s0);
  not not_6 (not_6_out, state_register_2bit_1_s1);
  not not_7 (not_7_out, p3s);
  not not_8 (not_8_out, state_register_2bit_1_s0);
  not not_9 (not_9_out, p37s);
  not not_10 (not_10_out, state_register_2bit_1_s1);
  not not_11 (not_11_out, state_register_2bit_1_s0);
  not not_12 (not_12_out, req);
  not not_13 (not_13_out, state_register_2bit_1_s1);
  not not_14 (not_14_out, state_register_2bit_1_s0);
  not not_15 (not_15_out, state_register_2bit_1_s1);
  not not_16 (not_16_out, p3s);
  not not_17 (not_17_out, state_register_2bit_1_s1);
  not not_18 (not_18_out, state_register_2bit_1_s0);
  not not_19 (not_19_out, p7s);
  not not_20 (not_20_out, state_register_2bit_1_s0);
  not not_21 (not_21_out, p37s);
  and and_1 (and_1_out, not_1_out, state_register_2bit_1_s0, p3s);
  and and_2 (and_2_out, state_register_2bit_1_s1, not_2_out);
  and and_3 (and_3_out, state_register_2bit_1_s1, state_register_2bit_1_s0, not_3_out);
  and and_4 (and_4_out, not_4_out, not_5_out, req);
  and and_5 (and_5_out, not_6_out, state_register_2bit_1_s0, not_7_out);
  and and_6 (and_6_out, state_register_2bit_1_s1, not_8_out, p7s);
  and and_7 (and_7_out, state_register_2bit_1_s1, state_register_2bit_1_s0, not_9_out);
  and and_8 (resetT, not_10_out, not_11_out, not_12_out);
  and and_9 (and_9_out, not_13_out, not_14_out);
  and and_10 (and_10_out, not_15_out, state_register_2bit_1_s0, not_16_out);
  and and_11 (and_11_out, state_register_2bit_1_s1, state_register_2bit_1_s0, p37s);
  and and_12 (and_12_out, not_17_out, p3s, state_register_2bit_1_s0);
  and and_13 (and_13_out, state_register_2bit_1_s1, not_18_out, not_19_out);
  and and_14 (and_14_out, state_register_2bit_1_s1, not_20_out, p7s);
  and and_15 (and_15_out, state_register_2bit_1_s1, state_register_2bit_1_s0, not_21_out);
  // OR_Gate n1 has open pins: in0=and_1_out, in1=and_2_out, in2=and_3_out, out=open
  // OR_Gate n0 has open pins: in0=and_4_out, in1=and_5_out, in2=and_6_out, in3=and_7_out, out=open
  or or_1 (or_1_out, and_9_out, and_10_out, and_11_out);
  or or_2 (or_2_out, and_12_out, and_13_out);
  or or_3 (or_3_out, and_14_out, and_15_out);
  LED redL (.in(or_1_out));
  LED orangeL (.in(or_2_out));
  LED greenL (.in(or_3_out));

  // Notes on the sheet:
  //   s0
  //   s1
endmodule

module state_register_2bit (
  input  clk,
  input  n1,
  input  n0,
  output s1,
  output s0
);

  D_Flip_Flop d_ff_1 (.clk(clk), .D(n1), .Q(s1), .en(1'b1));  // open: Qn, preset, reset
  D_Flip_Flop d_ff_2 (.clk(clk), .D(n0), .Q(s0), .en(1'b1));  // open: Qn, preset, reset
endmodule
