// Logisim project 161044119_lab6.circ as structural Verilog: 1 circuit, main circuit main
module main (
  input  [7:0] xi,
  input  [7:0] yi,
  input  [7:0] z,
  input  goi,
  output z_2
);

  wire [7:0] diff_q, subtractor_1_out;

  Subtractor subtractor_1 (.a(xi), .b(yi), .out(subtractor_1_out));  // open: bin, bout
  Register diff (.D(subtractor_1_out), .Q(diff_q));  // open: en, clk, clr
  Register diff2 (.D(diff_q));  // open: en, Q, clk, clr
  Comparator comparator_1 (.a(diff_q), .b({8{1'b0}}));  // open: gt, eq, lt
endmodule
